# Fritzing sketch labyrint_pcb_v1 (saved by Fritzing 0.9.3b)
circuit board: 7cm x 7.5cm
breadboards: 1

parts:
  OLED_SD1306 = Module display OLED I2C 128x64 SSD1306 [package=THT]
  yServo = Basic Servo
  xServo = Basic Servo
  FTDI232 = FTDI Basic Programmer
  h_t1 = female pin header, 21 pins [form="♀ (female)"]  # not connected
  h_t2 = female pin header, 21 pins [form="♀ (female)"]  # not connected
  h_b2 = female pin header, 21 pins [form="♀ (female)"]
  h_b1 = female pin header, 21 pins [form="♀ (female)"]
  BNO055 = 9-DOF Absolute Orientation IMU Fusion Breakout - BNO055

nets:
  GND: OLED_SD1306.GND, yServo.gnd, xServo.gnd, FTDI232.GND, h_b1.pin2, BNO055.GND
  VCC: OLED_SD1306.VCC, yServo.vcc, xServo.vcc, FTDI232.POWER, h_b1.pin3, BNO055.5.0V
  N1: OLED_SD1306.SCL, h_b2.pin16, BNO055.SCL_5V
  N2: OLED_SD1306.SDA, h_b1.pin16, BNO055.SDA_5V
  N3: yServo.pulse, h_b1.pin9
  N4: xServo.pulse, h_b2.pin9
  N5: FTDI232.RXI, h_b1.pin15
  N6: FTDI232.TXO, h_b2.pin15

notes:
  GND
  VCC
  ~
  SDA
  SCL
  Mega 2560 PRO (Embed)
  CH340G/ATmega2560-16AU
  Labyrinth controller board
  version 1
  Knowit Hardware Guild
  May 2019

custom parts:
  Module display OLED I2C 128x64 SSD1306: Ecran OLED I2C SSD163 de 128x64 avec connexion I2C
  9-DOF Absolute Orientation IMU Fusion Breakout - BNO055: A MEMS accelerometer, magnetometer and gyroscope on a single die with a high speed ARM Cortex-M0 based processor to digest all the sensor data, abstract the sensor fusion and real time requirements away, and spit out data you can use in quaternions, Euler angles or vectors.
